# Fritzing sketch brows-arduino (saved by Fritzing 0.9.0b)
breadboards: 1

parts:
  IC1 = L293D [package=THT]
  IR1 = TSOP312.., 314.. [package=THT]
  M1 = DC Motor
  M2 = DC Motor
  Part1 = Arduino Uno (Rev3)

nets:
  N1: IC1.In_1, Part1.D3_PWM
  N2: IC1.Out_1_(_Controlled_by_Enable_1_), M1.pin_2
  GND: IC1.0V, IR1.GND, Part1.GND
  N3: IC1.Out_2_(_Controlled_by_Enable_1_), M1.pin_1
  N4: IC1.In_2, Part1.D5_PWM
  N5: IC1.+Vmotor, IC1.+V, IR1.Vs, Part1.5V
  N6: IC1.In_3, Part1.D2
  N7: IC1.Out_3_(_Controlled_by_Enable_2_), M2.pin_2
  N8: IC1.Out_4_(_Controlled_by_Enable_2_), M2.pin_1
  N9: IC1.In_4, Part1.D4
  N10: IR1.Data, Part1.D10_PWM/SS
