# Fritzing sketch brows (saved by Fritzing 0.9.0b)
breadboards: 1

parts:
  U1 = atmega328 [package=dip]
  IC1 = L293D [package=THT]
  IR1 = TSOP312.., 314.. [package=THT]
  M1 = DC Motor
  M2 = DC Motor
  BATT1 = 3xAAA Switchable Battery Pack w/Bare Wire

nets:
  N1: U1.D2, IC1.In_3
  N2: U1.D3_(PWM), IC1.In_1
  N3: U1.D4, IC1.In_4
  N4: U1.VCC, U1.AVCC, IC1.+Vmotor, IC1.+V, IR1.Vs, BATT1.POS
  GND: U1.GND, IC1.0V, IR1.GND, BATT1.NEG
  N5: U1.D5_(PWM), IC1.In_2
  N6: U1.D10_(PWM), IR1.Data
  N7: IC1.Out_1_(_Controlled_by_Enable_1_), M1.pin_2
  N8: IC1.Out_2_(_Controlled_by_Enable_1_), M1.pin_1
  N9: IC1.Out_3_(_Controlled_by_Enable_2_), M2.pin_2
  N10: IC1.Out_4_(_Controlled_by_Enable_2_), M2.pin_1

custom parts:
  3xAAA Switchable Battery Pack w/Bare Wire: 3xAAA Switchable Battery Pack w/Bare Wire Connectors
